// Logisim project 转BCD.circ as structural Verilog: 1 circuit, main circuit main
module main (
  input  Y0,
  input  Y1,
  input  Y2,
  input  Y3,
  input  Y4,
  input  Y5,
  input  Y6,
  input  Y7,
  output A,
  output B,
  output C,
  output D
);

  wire not_1_out, not_2_out, not_3_out, not_4_out;

  not not_1 (not_1_out, Y0);
  not not_2 (not_2_out, Y1);
  not not_3 (not_3_out, Y2);
  not not_4 (not_4_out, Y4);
  and and_1 (D, not_1_out, not_2_out, not_3_out, not_4_out);

  assign A = Y1;
  assign B = Y2;
  assign C = Y4;
endmodule
